# Fritzing sketch rgb-led-strips (saved by Fritzing 0.9.5d)

parts:
  WeMos_D1_Mini1 = WeMos D1 Mini
  C1_100uF = Electrolytic Capacitor [capacitance=1μF package="0405 [SMD, electrolytic]"]
  RGB_SMD_LED1 = SMD RGB LED (WS2812B) [package=5050]
  Part1 = Logic Level Converter
  R1_100_Ohm = Resistor [package="2010 [SMD]"]
  GND_+5V = Camdenboss CTB0158-2 [part_number=CTB0158-2 package=THT]  # not connected
  U1 = LuaNode32 / ESP32 [part_number=ESP32S-PIN30]
  Part2 = Logic Level Converter
  GND_+12V = Camdenboss CTB0158-2 [part_number=CTB0158-2 package=THT]
  RGB_SMD_LED2 = SMD RGB LED (WS2812B) [package=5050]
  R1_100_Ohm_2 = Resistor [package="2010 [SMD]"]
  IC1 = Voltage Regulator [package=to-220-alt]  # not connected
  part = female pin header, 1 pin [form="♀ (female)"]  # not connected

nets:
  N1: WeMos_D1_Mini1.3V3, Part1.LV
  5V: WeMos_D1_Mini1.5V, C1_100uF.+, RGB_SMD_LED1.VDD
  N2: WeMos_D1_Mini1.D4, Part1.TX_LV
  N3: WeMos_D1_Mini1.G, C1_100uF.-, RGB_SMD_LED1.VSS
  N4: RGB_SMD_LED1.DIN, R1_100_Ohm.Pin_1
  N5: Part1.RX_HV, R1_100_Ohm.Pin_0
  N6: U1.Vin, Part2.HV
  N7: U1.3V3, Part2.LV
  N8: U1.D15, U1.D2, Part2.TX_LV
  N9: Part2.GND, GND_+12V.pin1
  N10: Part2.RX_HV, R1_100_Ohm_2.Pin_0
  N11: GND_+12V.pin2, RGB_SMD_LED2.VDD
  N12: RGB_SMD_LED2.DIN, R1_100_Ohm_2.Pin_1

notes:
  RGB-LED-STRIPS by luk6xff (2021)
  ESP8266 (D1 MINI)
  RGB LEDS WS2812 (5V)
  ESP32 DEV (WEMOS WROOM32)
  RGB LEDS WS2811 (12V)

custom parts:
  SMD RGB LED (WS2812B): The WS2812B is an RGB LED with a WS2811 control IC built right into the LED. Its improvement over its WS2812 ancestor is the reduction to 4 pins (a single power supply instead of 2) and dropping the requirement for the external resistors. The manufacturer says it has a better reverse connect protection.
  Resistor: Resistor Basic schematic elements and footprints for 0603, 1206, and PTH resistors.
  LuaNode32 / ESP32: New Image for LuaNode32 DOIT ESP32 DEVKIT V1. Base parts from LuaNode32 / ESP32 ESP32 based LuaNode32 by G.Noorlander DOIT Esp32 DevKit v1 (30 pins long, 11 pins width) by Werner Rothschopf (modified by vanepp Dec 2018)
